// Logisim project traffics_lights.circ as structural Verilog: 4 circuits, main circuit main
module main (
  input  Sensor,
  input  \Botão 
);

  wire and_1_out, clock_1_out, counter_1_carry, d_ff_1_q, d_ff_2_q, demultiplexer_1_out0,
       demultiplexer_1_out1, demultiplexer_1_out2, demultiplexer_1_out3, demultiplexer_1_out4,
       demultiplexer_1_out5, demultiplexer_1_out6, demultiplexer_1_out7, demultiplexer_1_out8,
       demultiplexer_1_out9, demultiplexer_1_out10, demultiplexer_1_out11, demultiplexer_1_out12,
       demultiplexer_1_out13, demultiplexer_2_out0, demultiplexer_2_out1, demultiplexer_2_out2,
       demultiplexer_2_out3, demultiplexer_2_out4, demultiplexer_2_out5, demultiplexer_2_out6,
       demultiplexer_2_out7, demultiplexer_2_out8, demultiplexer_2_out9, demultiplexer_2_out10,
       demultiplexer_2_out11, demultiplexer_2_out12, demultiplexer_2_out13, demultiplexer_3_out0,
       demultiplexer_3_out1, demultiplexer_4_out0, demultiplexer_4_out1, or_1_out, or_2_out, or_3_out,
       or_4_out, or_5_out, or_6_out, or_7_out, or_8_out, or_9_out, or_10_out, or_11_out, or_12_out,
       or_13_out, or_14_out, or_15_out;
  wire [3:0] counter_1_q;

  Clock clock_1 (.out(clock_1_out));
  D_Flip_Flop d_ff_1 (.clk(\Botão ), .D(\Botão ), .Q(d_ff_1_q));  // open: Qn, preset, en, reset
  D_Flip_Flop d_ff_2 (.clk(Sensor), .D(Sensor), .Q(d_ff_2_q));  // open: Qn, preset, en, reset
  Counter #(.width(4), .max('hf)) counter_1 (
    .Q(counter_1_q), .carry(counter_1_carry), .clk(clock_1_out), .clr(or_1_out));  // open: load, D, count
  Demultiplexer #(.select(4)) demultiplexer_1 (
    .out0(demultiplexer_1_out0), .out1(demultiplexer_1_out1), .out2(demultiplexer_1_out2),
    .out3(demultiplexer_1_out3), .out4(demultiplexer_1_out4), .out5(demultiplexer_1_out5),
    .out6(demultiplexer_1_out6), .out7(demultiplexer_1_out7), .out8(demultiplexer_1_out8),
    .out9(demultiplexer_1_out9), .out10(demultiplexer_1_out10), .out11(demultiplexer_1_out11),
    .out12(demultiplexer_1_out12), .out13(demultiplexer_1_out13), .in(d_ff_2_q), .sel(counter_1_q));  // open: out14, out15, en
  or or_1 (or_1_out, demultiplexer_1_out13, and_1_out, demultiplexer_2_out13);
  Demultiplexer #(.select(4)) demultiplexer_2 (
    .out0(demultiplexer_2_out0), .out1(demultiplexer_2_out1), .out2(demultiplexer_2_out2),
    .out3(demultiplexer_2_out3), .out4(demultiplexer_2_out4), .out5(demultiplexer_2_out5),
    .out6(demultiplexer_2_out6), .out7(demultiplexer_2_out7), .out8(demultiplexer_2_out8),
    .out9(demultiplexer_2_out9), .out10(demultiplexer_2_out10), .out11(demultiplexer_2_out11),
    .out12(demultiplexer_2_out12), .out13(demultiplexer_2_out13), .in(d_ff_1_q), .sel(counter_1_q));  // open: out14, out15, en
  or or_2 (or_2_out, demultiplexer_2_out3, demultiplexer_2_out5, demultiplexer_2_out6, demultiplexer_2_out7, demultiplexer_2_out8, demultiplexer_2_out9);
  or or_3 (or_3_out, demultiplexer_2_out9, demultiplexer_2_out5, demultiplexer_2_out3);
  Demultiplexer demultiplexer_3 (
    .out0(demultiplexer_3_out0), .out1(demultiplexer_3_out1), .in(demultiplexer_1_out1), .sel(or_6_out));  // open: en
  or or_4 (or_4_out, demultiplexer_1_out3, demultiplexer_1_out4, demultiplexer_1_out5, demultiplexer_1_out6, demultiplexer_1_out7, demultiplexer_1_out8, demultiplexer_1_out9, demultiplexer_1_out10, demultiplexer_1_out11, demultiplexer_1_out12);
  and and_1 (and_1_out, demultiplexer_3_out0, demultiplexer_4_out0);
  or or_5 (or_5_out, demultiplexer_2_out7, demultiplexer_2_out6, demultiplexer_2_out5, demultiplexer_2_out3);
  or or_6 (or_6_out, Sensor, \Botão );
  or or_7 (or_7_out, demultiplexer_2_out8, demultiplexer_2_out9, demultiplexer_2_out6, demultiplexer_2_out5, demultiplexer_2_out3);
  or or_8 (or_8_out, demultiplexer_1_out0, demultiplexer_3_out0);
  or or_9 (or_9_out, demultiplexer_3_out1, demultiplexer_1_out2);
  or or_10 (or_10_out, demultiplexer_2_out9, demultiplexer_2_out8, demultiplexer_2_out6, demultiplexer_2_out5, demultiplexer_2_out4, demultiplexer_2_out3);
  LED V_Verde (.in(or_8_out));
  LED V_Amarelo (.in(or_9_out));
  LED V_Vermelho (.in(or_4_out));
  or or_11 (or_11_out, demultiplexer_2_out10, demultiplexer_2_out9, demultiplexer_2_out8, demultiplexer_2_out7, demultiplexer_2_out4, demultiplexer_2_out3);
  or or_12 (or_12_out, demultiplexer_2_out3, demultiplexer_2_out4, demultiplexer_2_out5, demultiplexer_2_out6, demultiplexer_2_out7, demultiplexer_2_out8, demultiplexer_2_out9, demultiplexer_2_out10);
  or or_13 (or_13_out, demultiplexer_2_out10, demultiplexer_2_out8, demultiplexer_2_out7, demultiplexer_2_out6, demultiplexer_2_out5, demultiplexer_2_out4, demultiplexer_2_out3);
  Demultiplexer demultiplexer_4 (
    .out0(demultiplexer_4_out0), .out1(demultiplexer_4_out1), .in(demultiplexer_2_out1), .sel(\Botão ));  // open: en
  or or_14 (or_14_out, demultiplexer_2_out11, demultiplexer_2_out12);
  or or_15 (or_15_out, demultiplexer_2_out0, demultiplexer_4_out0, demultiplexer_4_out1, demultiplexer_2_out2);
  _7_Segment_Display u_7_segment_display_1 (
    .g(or_2_out), .f(or_5_out), .a(or_10_out), .b(or_11_out), .e(or_3_out), .d(or_7_out), .c(or_13_out));  // open: dp
  LED P_Vermelho (.in(or_15_out));
  LED P_Amarelo (.in(or_14_out));
  LED P_Verde (.in(or_12_out));

  // Notes on the sheet:
  //   select - contador
  //   select - contador
  //   porta OR para reset ao contador, e ao circuito
  //   porta OR - sensor ou saída 0 DMX Botão
  //   porta AND para que o circuito avaçe para além de output 0
  //   1 impulso
  //   2 impulsos
  //   10 impulsos
  //   uma porta OR por segmento do display
  //   13 impulsos (+ 1 reset)
  //   3 impulsos
  //   2 impulsos
  //   8 impulsos
  //   13 impulosos 8+ 1 reset)
endmodule

module _1 (
  input  in_1,
  output out_2
);


  assign out_2 = in_1;
endmodule

module _2 (
  input  in_1,
  output out_2
);


  assign out_2 = in_1;
endmodule

module simple_main (
  input  Sensor,
  input  Button,
  output V_VERDE,
  output V_AMARELO,
  output V_VERMELHO,
  output P_VERMELHO,
  output P_AMARELO,
  output P_VERDE
);

  wire and_1_out, and_2_out, not_1_out, not_2_out, not_3_out, not_4_out;

  not not_1 (not_1_out, Sensor);
  not not_2 (not_2_out, Button);
  not not_3 (not_3_out, Sensor);
  not not_4 (not_4_out, Button);
  and and_1 (and_1_out, not_1_out, not_2_out);
  and and_2 (and_2_out, Sensor, Button);
  and and_3 (P_VERMELHO, not_3_out, not_4_out);
  or or_1 (V_VERDE, and_1_out, and_2_out);

  assign P_AMARELO = 1'b0;
  assign P_VERDE = 1'b0;
  assign V_AMARELO = Sensor;
  assign V_VERMELHO = Sensor;
endmodule
